// Logisim project Projeção circuitos.circ as structural Verilog: 4 circuits, main circuit somador completo
module somador_completo (
  input  C_in,
  input  A,
  input  C_in_2,
  input  Entrada_A,
  input  B,
  input  Entrada_B,
  input  C_in_3,
  input  [7:0] Entrada_A_2,
  input  [7:0] Entrada_B_2,
  input  C_in_4,
  input  A_2,
  input  A_3,
  input  A_4,
  input  A_5,
  input  A_6,
  input  A_7,
  input  A_8,
  input  A_9,
  input  B_2,
  input  B_3,
  input  B_4,
  input  B_5,
  input  B_6,
  input  B_7,
  input  B_8,
  input  B_9,
  output Saida,
  output Saida_2,
  output OVERFLOW,
  output C_out,
  output [7:0] Saida_3,
  output OVERFLOW_2,
  output out_33,
  output out_34,
  output out_35,
  output out_36,
  output out_37,
  output out_38,
  output out_39,
  output out_40,
  output out_41
);

  wire adder_1_cout, adder_4_cout, adder_5_cout, adder_6_cout, adder_7_cout, adder_8_cout, adder_9_cout,
       adder_10_cout, and_1_out, and_2_out, and_3_out, xor_1_out;

  Adder #(.width(1)) adder_1 (.a(A_2), .b(B_2), .out(out_33), .cin(C_in_4), .cout(adder_1_cout));
  Adder #(.width(1)) adder_2 (.a(Entrada_A), .b(Entrada_B), .out(Saida_2), .cin(C_in_2), .cout(OVERFLOW));
  Adder adder_3 (.a(Entrada_A_2), .b(Entrada_B_2), .out(Saida_3), .cin(C_in_3), .cout(OVERFLOW_2));
  Adder #(.width(1)) adder_4 (.a(A_3), .b(B_3), .out(out_34), .cin(adder_1_cout), .cout(adder_4_cout));
  Adder #(.width(1)) adder_5 (.a(A_4), .b(B_4), .out(out_35), .cin(adder_4_cout), .cout(adder_5_cout));
  Adder #(.width(1)) adder_6 (.a(A_5), .b(B_5), .out(out_36), .cin(adder_5_cout), .cout(adder_6_cout));
  xor xor_1 (xor_1_out, A, B);
  Adder #(.width(1)) adder_7 (.a(A_6), .b(B_6), .out(out_37), .cin(adder_6_cout), .cout(adder_7_cout));
  and and_1 (and_1_out, C_in, A);
  and and_2 (and_2_out, C_in, B);
  and and_3 (and_3_out, B, A);
  xor xor_2 (Saida, xor_1_out, C_in);
  Adder #(.width(1)) adder_8 (.a(A_7), .b(B_7), .out(out_38), .cin(adder_7_cout), .cout(adder_8_cout));
  or or_1 (C_out, and_1_out, and_2_out, and_3_out);
  Adder #(.width(1)) adder_9 (.a(A_8), .b(B_8), .out(out_39), .cin(adder_8_cout), .cout(adder_9_cout));
  Adder #(.width(1)) adder_10 (.a(A_9), .b(B_9), .out(out_40), .cin(adder_9_cout), .cout(adder_10_cout));
  xor xor_3 (out_41, adder_10_cout, adder_9_cout);

  // Notes on the sheet:
  //   Somador de 1 bits
  //   Somador de 8 bits
  //   Circuito Somador de 8 bits
  //   Circuito Somador de 1 bit
  //   OVERFLOW
endmodule

module Subtrator_completo (
  input  Bit_0,
  input  [7:0] Entrada_A,
  input  in_3,
  input  Bit_1,
  input  C_in,
  input  [7:0] Soma_1_no_C2,
  input  Bit_2,
  input  Bit_3,
  input  Bit_4,
  input  [7:0] Entrada_B,
  input  Bit_5,
  input  Bit_6,
  input  Bit_7,
  input  Entrada_A_2,
  input  Entrada_B_2,
  input  B_in__Borrow_in,
  output Bit_0_2,
  output Bit_1_2,
  output Bit_2_2,
  output C_out__desconsiderado,
  output [7:0] Saida,
  output Bit_3_2,
  output Bit_4_2,
  output OVERFLOW,
  output Bit_5_2,
  output Bit_6_2,
  output Bit_7_2,
  output B_out__Borrow_out,
  output Saida_2
);

  wire and_1_out, and_2_out, not_1_out, not_3_out, xor_1_out;
  wire [7:0] adder_1_out, not_2_out;

  not not_1 (not_1_out, Entrada_A_2);
  assign not_2_out = ~Entrada_A;  // NOT_Gate not_2, 8 bits wide
  Adder adder_1 (.a(not_2_out), .b(Soma_1_no_C2), .out(adder_1_out), .cin(in_3), .cout(C_out__desconsiderado));
  and and_1 (and_1_out, not_1_out, Entrada_B_2);
  xor xor_1 (xor_1_out, Entrada_A_2, Entrada_B_2);
  not not_3 (not_3_out, xor_1_out);
  and and_2 (and_2_out, not_3_out, B_in__Borrow_in);
  xor xor_2 (Saida_2, xor_1_out, B_in__Borrow_in);
  Adder adder_2 (.a(adder_1_out), .b(Entrada_B), .out(Saida), .cin(C_in), .cout(OVERFLOW));
  or or_1 (B_out__Borrow_out, and_1_out, and_2_out);
  not not_4 (Bit_0_2, Bit_0);
  not not_5 (Bit_1_2, Bit_1);
  not not_6 (Bit_2_2, Bit_2);
  not not_7 (Bit_3_2, Bit_3);
  not not_8 (Bit_4_2, Bit_4);
  not not_9 (Bit_5_2, Bit_5);
  not not_10 (Bit_6_2, Bit_6);
  not not_11 (Bit_7_2, Bit_7);

  // Notes on the sheet:
  //   INVERSOR
  //   Circuito Subtrator de 1 bit
  //   Circuito Subtrator de 8 bits
  //   Somador de 8 bits
  //   Circuito Inversor de 8 bits
endmodule

module MUX_add_sub (
  input  Entrada_A,
  input  Entrada_B,
  input  SELECT,
  input  [7:0] Entrada_A_2,
  input  [7:0] Entrada_B_2,
  input  SELECT_2,
  output Saida,
  output C_out,
  output [7:0] Saida_2,
  output OVERFLOW
);

  wire multiplexer_1_out, not_1_out;
  wire [7:0] multiplexer_2_out, not_2_out;

  Multiplexer #(.enable("false")) multiplexer_1 (
    .in0(Entrada_B), .in1(not_1_out), .out(multiplexer_1_out), .sel(SELECT));
  not not_1 (not_1_out, Entrada_B);
  Multiplexer #(.width(8), .enable("false")) multiplexer_2 (
    .in0(Entrada_B_2), .in1(not_2_out), .out(multiplexer_2_out), .sel(SELECT_2));
  assign not_2_out = ~Entrada_B_2;  // NOT_Gate not_2, 8 bits wide
  Adder adder_1 (.a(Entrada_A_2), .b(multiplexer_2_out), .out(Saida_2), .cin(SELECT_2), .cout(OVERFLOW));
  Adder #(.width(1)) adder_2 (.a(Entrada_A), .b(multiplexer_1_out), .out(Saida), .cin(SELECT), .cout(C_out));

  // Notes on the sheet:
  //   Somador / Subtrator de 1 bit
  //   Somador / Subtrator de 8 bits
endmodule

module mux_2x1_e_2x8 (
  input  C0,
  input  SELECT,
  input  C1,
  input  C0_2,
  input  [7:0] C0_3,
  input  C1_2,
  input  [7:0] C1_3,
  input  SELECT_2,
  input  SELECT_3,
  output Z,
  output Z_2,
  output [7:0] Z_3
);

  wire and_1_out, and_2_out, not_1_out;

  Multiplexer #(.enable("false")) multiplexer_1 (.in0(C0_2), .in1(C1_2), .out(Z_2), .sel(SELECT_2));
  not not_1 (not_1_out, SELECT);
  and and_1 (and_1_out, C0, not_1_out);
  and and_2 (and_2_out, SELECT, C1);
  Multiplexer #(.width(8), .enable("false")) multiplexer_2 (.in0(C0_3), .in1(C1_3), .out(Z_3), .sel(SELECT_3));
  or or_1 (Z, and_1_out, and_2_out);

  // Notes on the sheet:
  //   Módulo MUX2x1
  //   Circuito  MUX2x1
  //   Módulo MUX2x8
endmodule
